# Fritzing sketch Super_Knob_Circuit (saved by Fritzing 0.9.3b)
breadboards: 1

parts:
  R1 = Trimmer Potentiometer [maximum_resistance=10kΩ package=THT]
  R2 = Trimmer Potentiometer [maximum_resistance=10kΩ package=THT]
  R3 = Trimmer Potentiometer [maximum_resistance=10kΩ package=THT]
  Part1 = Arduino Uno (Rev3) - ICSP
  J1 = Basic Servo

nets:
  GND: R1.leg1, R2.leg1, R3.leg1, Part1.GND, J1.gnd
  N1: R1.wiper, Part1.A1
  5V: R1.leg2, R2.leg2, R3.leg2, Part1.5V, J1.vcc
  N2: R2.wiper, Part1.A2
  N3: R3.wiper, Part1.A0
  N4: Part1.D9_PWM, J1.pulse
